# Fritzing sketch Esquemas1 (saved by Fritzing 0.9.2b)
breadboards: 1

parts:
  Parte2 = Arduino Uno (Rev3) - ICSP
  Parte3 = LCD1602-I2C
  Parte4 = FC-28 Soil Hygrometer Module - Probe
  Parte5 = FC-28 Soil Hygrometer Module

nets:
  N1: Parte2.A1, Parte5.AO
  N2: Parte2.A4/SDA, Parte3.SDA
  N3: Parte2.A5/SCL, Parte3.SCL
  VCC: Parte2.5V, Parte3.VCC, Parte5.VCC
  GND: Parte2.GND, Parte3.GND, Parte5.GND
  N4: Parte4.POS, Parte5.POS
  N5: Parte4.NEG, Parte5.NEG

notes:
  LCD 1602- IC2
  - GND: Protoboard
  - VCC: Protoboard
  -SDA: Pin SDA
  - SCL: Pin SCL
  FC - 28 Sensor de humedad de suelo
  - Postivo
  - Negativo
  FC 28- Módulo de Sensor de humedad de suelo
  - VCC: Protoboard
  - GND: Protoboard
  - AO: Pin A1

custom parts:
  LCD1602-I2C: A standard character display, usually with 2x16 characters. Comes in many colors with LCM1602 IIC attached.
  FC-28 Soil Hygrometer Module - Probe: The FC-28 is a soil hygrometer module that uses the Texas Instruments LM393 comparator chip to provide an analog measurement of soil humidity.
  FC-28 Soil Hygrometer Module: The FC-28 is a soil hygrometer module that uses the Texas Instruments LM393 comparator chip to provide an analog measurement of soil humidity. The digital output is high when soil moisture is over a certain threshold, as determined by adjusting the potentiometer.
