# Fritzing sketch Esquemas2 (saved by Fritzing 0.9.2b)
breadboards: 2

parts:
  Parte2 = Arduino Uno (Rev3) - ICSP
  LED1 = smd LED [color="Red (633nm)" package="0805 [SMD]"]
  LED2 = smd LED [color="Blue (525nm)" package="0805 [SMD]"]
  Parte3 = LCD1602-I2C
  Parte4 = FC-28 Soil Hygrometer Module - Probe
  Parte5 = FC-28 Soil Hygrometer Module
  R1 = Resistor [tolerance=±5% resistance=220 package="0402 [SMD]"]
  R2 = Resistor [tolerance=±5% resistance=220 package="0402 [SMD]"]

nets:
  N1: Parte2.A1, Parte5.AO
  N2: Parte2.A4/SDA, Parte3.SDA
  N3: Parte2.A5/SCL, Parte3.SCL
  N4: Parte2.D3_PWM, LED1.anode
  N5: Parte2.D4, LED2.anode
  VCC: Parte2.5V, Parte3.VCC, Parte5.VCC
  GND: Parte2.GND, Parte3.GND, Parte5.GND, R1.Pin_1, R2.Pin_1
  N6: LED1.cathode, R1.Pin_0
  N7: LED2.cathode, R2.Pin_0
  N8: Parte4.POS, Parte5.POS
  N9: Parte4.NEG, Parte5.NEG

notes:
  LCD 1602- IC2
  - GND: Protoboard
  - VCC: Protoboard
  -SDA: Pin SDA
  - SCL: Pin SCL
  FC - 28 Sensor de humedad de suelo
  - Postivo
  - Negativo
  FC 28- Módulo de Sensor de humedad de suelo
  - VCC: Protoboard
  - GND: Protoboard
  - AO: Pin A1
  Led Rojo
  - GND: R 220
  - Pin 3
  Led Azul
  - GND: R 220
  - Pin 4

custom parts:
  LCD1602-I2C: A standard character display, usually with 2x16 characters. Comes in many colors with LCM1602 IIC attached.
  FC-28 Soil Hygrometer Module - Probe: The FC-28 is a soil hygrometer module that uses the Texas Instruments LM393 comparator chip to provide an analog measurement of soil humidity.
  FC-28 Soil Hygrometer Module: The FC-28 is a soil hygrometer module that uses the Texas Instruments LM393 comparator chip to provide an analog measurement of soil humidity. The digital output is high when soil moisture is over a certain threshold, as determined by adjusting the potentiometer.
