# Fritzing sketch EsquemasFinal (saved by Fritzing 0.9.2b)
breadboards: 2

parts:
  Parte1 = Matrix LED de 8x8 basada en MAX7219
  Parte2 = Arduino Uno (Rev3) - ICSP
  LED1 = smd LED [color="Red (633nm)" package="0805 [SMD]"]
  LED2 = smd LED [color="Blue (525nm)" package="0805 [SMD]"]
  J1 = Piezo Speaker
  Parte3 = LCD1602-I2C
  Parte4 = FC-28 Soil Hygrometer Module - Probe
  WATER_PUMP1 = water pump/motor
  Parte5 = FC-28 Soil Hygrometer Module
  R1 = Resistor [tolerance=±5% resistance=220 package="0402 [SMD]"]
  R2 = Resistor [tolerance=±5% resistance=220 package="0402 [SMD]"]
  Mod1 = KY-019 5V Relay Module [package="Breakout board"]
  VCC1 = Battery block 9V

nets:
  VCC: Parte1.VCC, Parte2.5V, Parte3.VCC, Parte5.VCC, Mod1.+
  GND: Parte1.GND, Parte2.GND, J1.pin1, Parte3.GND, Parte5.GND, R1.Pin_1, R2.Pin_1, Mod1.-, VCC1.-
  N1: Parte1.CS, Parte2.D10_PWM/SS
  N2: Parte1.CLK, Parte2.ICSP_MOSI, Parte2.D11_PWM/MOSI
  N3: Parte1.DIN, Parte2.ICSP_MISO, Parte2.D12/MISO
  N4: Parte2.A1, Parte5.AO
  N5: Parte2.D8, J1.pin2
  N6: Parte2.D9_PWM, Mod1.S
  N7: Parte2.A4/SDA, Parte3.SDA
  N8: Parte2.A5/SCL, Parte3.SCL
  N9: Parte2.D3_PWM, LED1.anode
  N10: Parte2.D4, LED2.anode
  N11: LED1.cathode, R1.Pin_0
  N12: LED2.cathode, R2.Pin_0
  N13: Parte4.POS, Parte5.POS
  N14: Parte4.NEG, Parte5.NEG
  N15: WATER_PUMP1.pin_2, Mod1.NO

notes:
  Matriz 72198X8
  VCC. Protoboard
  GND: Protoboard
  DIN: Pin12
  ClK: Pin 11
  CS: Pin 10
  LCD 1602- IC2
  - GND: Protoboard
  - VCC: Protoboard
  -SDA: Pin SDA
  - SCL: Pin SCL
  FC - 28 Sensor de humedad de suelo
  - Postivo
  - Negativo
  FC 28- Módulo de Sensor de humedad de suelo
  - VCC: Protoboard
  - GND: Protoboard
  - AO: Pin A1
  KY-019 5V Relay
  - VCC: Protoboard
  - GND: Protoboard
  - Pin 9
  Mini Bomba de agua sumergible
  - Positivo (+): Relay
  - Negativo(-): Transformador 5V
  Led Rojo
  - GND: R 220 ohms
  - Pin 3
  Led Azul
  - GND: R 220ohms
  - Pin 4
  Buzzer
  - GND: Protoboard
  - Pin 6
  Batería 9V
  - Alimenta placa arduino y protoboard
  Transformador de 5V
  Que alimenta la miniBomba
  - Negativo (-) al negativo de la minibomba
  - Positivo (+) al Releay

custom parts:
  LCD1602-I2C: A standard character display, usually with 2x16 characters. Comes in many colors with LCM1602 IIC attached.
  FC-28 Soil Hygrometer Module - Probe: The FC-28 is a soil hygrometer module that uses the Texas Instruments LM393 comparator chip to provide an analog measurement of soil humidity.
  water pump/motor: WATER PUMP BY ARDUBLOCKTR
  FC-28 Soil Hygrometer Module: The FC-28 is a soil hygrometer module that uses the Texas Instruments LM393 comparator chip to provide an analog measurement of soil humidity. The digital output is high when soil moisture is over a certain threshold, as determined by adjusting the potentiometer.
  KY-019 5V Relay Module: KY-019 5V Relay module, used to control AC circuits. (Special thanks to vanepp for fixing the PCB holes and other errors)
